# Fritzing sketch Schematic (saved by Fritzing 0.8.7b)
perfboards: 1

parts:
  Q1 = NPN-Transistor [package="TO92 [THT]"]
  PullDown = Resistor [tolerance=±5% resistance=10k package=THT]
  part = Resistor [tolerance=±5% resistance=1k package=THT]
  X1 = USB Connectors [package=usb-a-s-silk-female]

nets:
  GND: Q1.E, PullDown.Pin_0
  N1: Q1.B, PullDown.Pin_1, part.Pin_1
  N2: Q1.C, X1.GND
  3.3v Signal: part.Pin_0
  5V: X1.D+

notes:
  BC547
